// Logisim project Full adder.circ as structural Verilog: 1 circuit, main circuit main
module main (
  input  A,
  input  B,
  input  Carry_In,
  output out_4,
  output Carry
);

  wire and_1_out, and_2_out, and_3_out, xor_1_out;

  xor xor_1 (xor_1_out, A, B);
  and and_1 (and_1_out, A, B);
  and and_2 (and_2_out, B, Carry_In);
  and and_3 (and_3_out, A, Carry_In);
  xor xor_2 (out_4, xor_1_out, Carry_In);
  or or_1 (Carry, and_1_out, and_2_out, and_3_out);
endmodule
