// Logisim project Full adder.circ as structural Verilog: 1 circuit, main circuit main
module main (
  input  A,
  input  B,
  input  Borrow_In,
  output out_4,
  output Borrow_out
);

  wire and_1_out, and_2_out, and_3_out, not_1_out, xor_1_out;

  not not_1 (not_1_out, A);
  xor xor_1 (xor_1_out, A, B);
  and and_1 (and_1_out, not_1_out, B);
  and and_2 (and_2_out, B, Borrow_In);
  and and_3 (and_3_out, not_1_out, Borrow_In);
  xor xor_2 (out_4, xor_1_out, Borrow_In);
  or or_1 (Borrow_out, and_1_out, and_2_out, and_3_out);
endmodule
