// Logisim project D Flip-Flop.circ as structural Verilog: 1 circuit, main circuit main
module main (
  input  Din,
  output Q,
  output Q_prime
);

  wire Clock_out, nand_1_out, nand_2_out, not_1_out;

  Clock Clock (.out(Clock_out));
  not not_1 (not_1_out, Din);
  nand nand_1 (nand_1_out, Din, Clock_out);
  nand nand_2 (nand_2_out, Clock_out, not_1_out);
  nand nand_3 (Q, nand_1_out, Q_prime);
  nand nand_4 (Q_prime, Q, nand_2_out);
endmodule
