// Logisim project MOD-3 counter.circ as structural Verilog: 1 circuit, main circuit main
module main (
  output Q1,
  output Q0
);

  wire CLK_out, j_k_ff_2_qn;

  Clock CLK (.out(CLK_out));
  J_K_Flip_Flop j_k_ff_1 (.J(j_k_ff_2_qn), .clk(CLK_out), .K(1'b1), .Q(Q0));  // open: Qn, preset, en, reset
  J_K_Flip_Flop j_k_ff_2 (.J(Q0), .clk(CLK_out), .K(1'b1), .Q(Q1), .Qn(j_k_ff_2_qn));  // open: preset, en, reset

  // Notes on the sheet:
  //   VCC
endmodule
